# Fritzing sketch dispenser-with-just-resistors (saved by Fritzing 0.9.10b)
circuit board: 5.8cm x 4.5cm
perfboards: 1

parts:
  ESP32-30pin1 = esp32
  USB-S = Header 5x2 [package=2x5-ra]
  USB-ESP = Header 5x2 [package=2x5-ra]
  J1 = Basic Servo
  R13 = Resistor [tolerance=±20% power=0.25 resistance=22 package=THT]
  R20 = Resistor [tolerance=±20% power=0.25 resistance=100 package=THT]
  R21 = Resistor [tolerance=±20% power=0.25 resistance=100 package=THT]
  R22 = Resistor [tolerance=±20% power=0.25 resistance=220 package=THT]
  R23 = Resistor [tolerance=±20% power=0.25 resistance=1k package=THT]

nets:
  N1: ESP32-30pin1.d19, J1.pulse
  GND: ESP32-30pin1.gnd, ESP32-30pin1.GND, USB-S.1, USB-ESP.1, J1.gnd, R20.Pin_1, R21.Pin_1, R22.Pin_1, R23.Pin_1
  N2: ESP32-30pin1.Vin, USB-ESP.9, R13.Pin_0
  N3: USB-S.9, J1.vcc, R21.Pin_0, R22.Pin_0, R23.Pin_0
  N4: R13.Pin_1, R20.Pin_0

notes:
  resistor for servo. Servo doesn't take current at all in idle mode, so we need to take full 70mA through resistor
  resistor for esp32 circuit. I assume that esp32 takes 35mAh, so need to draw additional 35mAh

custom parts:
  esp32: based on work of Roman Minyaylov, at https://github.com/roman-minyaylov/nodemcu-v3-fritzing
